// Logisim project DDCA Source.circ as structural Verilog: 1 circuit, main circuit main
module main (
  input  in_1,
  input  in_2,
  input  in_3,
  input  in_4,
  output out_5,
  output out_6
);

  wire not_1_out, not_2_out;

  not not_1 (not_1_out, in_2);
  not not_2 (not_2_out, in_4);
  and and_1 (out_5, in_1, not_1_out, in_3, not_2_out);
  not not_3 (out_6, out_5);
endmodule
